# Fritzing sketch Diagram_pill_dispenser (saved by Fritzing 0.9.3b)

parts:
  CPU1 = NodeMCU WROOM ESP 32
  SERVO1 = Tower Pro SG90 servo [part_number=101246]
  SERVO2 = Tower Pro SG90 servo [part_number=101246]
  SERVO3 = Tower Pro SG90 servo [part_number=101246]
  SERVO4 = Tower Pro SG90 servo [part_number=101246]
  SERVO5 = Tower Pro SG90 servo [part_number=101246]
  YwRobot_Power_Supply1 = YwRobot Breadboard Power Supply [part_number=545043]

nets:
  N1: CPU1.pin_10, SERVO5.Signal
  N2: CPU1.pin_11, SERVO4.Signal
  N3: CPU1.pin_12, SERVO2.Signal
  N4: CPU1.pin_13, SERVO3.Signal
  N5: CPU1.pin_14, SERVO1.Signal
  GND: CPU1.pin_15, SERVO1.GND, SERVO2.GND, SERVO3.GND, SERVO4.GND, SERVO5.GND, YwRobot_Power_Supply1.GND
  +5V: CPU1.pin_16, SERVO1.+5V, SERVO2.+5V, SERVO3.+5V, SERVO4.+5V, SERVO5.+5V, YwRobot_Power_Supply1.VCC

custom parts:
  NodeMCU WROOM ESP 32: 30 pol Development Kit
  Tower Pro SG90 servo: Original file by John De Cristofaro http://www.adafruit.com/products/1449 Adafruit Feedback Servo (Small) Edited by: e-radionica.com 28/9/2015
  YwRobot Breadboard Power Supply: The YwRobot Breadboard Power Supply (MB-V2) has two power rails; they can be 5V or 3V3. Power to the module can be provided through the female USB socket or through the A10 (female) 2.1mm power jack.
